# Fritzing sketch OpenTholoMetri electrical layout (saved by Fritzing 1.0.6)

parts:
  Part1 = Adafruit VCNL4010 Proximity and Light sensor [part_number="Adafruit #466"]
  Part2 = Adafruit Feather M0 Basic Proto [part_number="Adafruit #2772"]
  R1 = Resistor [tolerance=±5% power=0.25W resistance=4.7k package=THT]
  ds18b20_probe1 = ds18b20 probe
  U1 = Turbidity Sensor Probe [package=THT]  # not connected
  JP1 = Header 4 [package=1x04-1mm-ra]
  J1 = female pin header, 1 pin [form="♀ (female)"]

nets:
  N1: Part1.SDA, Part2.SDA
  N2: Part1.SCL, Part2.SCL
  GND: Part1.GND, Part2.GND, ds18b20_probe1.pin3, JP1.1
  VIN: Part1.VIN, Part2.+3V3, Part2.N$39, Part2.N$40, R1.Pin_0
  N3: Part2.A1, JP1.4
  N4: Part2.A0, Part2.N$22, Part2.N$35, Part2.N$44, R1.Pin_1, ds18b20_probe1.pin2
  N5: Part2.D13, JP1.2
  N6: Part2.D12, ds18b20_probe1.pin1
  N7: Part2.D5, J1.pin1

custom parts:
  Adafruit VCNL4010 Proximity and Light sensor: The VCNL4010 sensor is a nice way to add a small-distance proximity sensor to your microcontroller project. For longer distances (in the range of cm, you can use a SHARP IR distance sensor, but those are only good if the object is over 10 cm away. The VCNL4010 is designed for much shorter distances, no more than 200mm (about 7.5") and under our experimentation we found it worked best at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
  Adafruit Feather M0 Basic Proto: At the Feather M0's heart is an ATSAMD21G18 ARM Cortex M0 processor, clocked at 48 MHz and at 3.3V logic, the same one used in the new Arduino Zero. This chip has a whopping 256K of FLASH (8x more than the Atmega328 or 32u4) and 32K of RAM (16x as much)! This chip comes with built in USB so it has USB-to-Serial program & debug capability built in with no need for an FTDI-like chip. To make it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
  Turbidity Sensor Probe: Turbidity sensor probe to the DFRobot measure module.
  Header 4: Header 4 Standard 4-pin 0.1 header. Use with straight break away headers (SKU : PRT-00116), right angle break away headers (PRT-00553), swiss pins (PRT-00743), machine pins (PRT-00117), and female headers (PRT-00115). Molex polarized connector foot print use with SKU : PRT-08231 with associated crimp pins and housings. 1MM SMD Version SKU: PRT-10208
